# Fritzing sketch purpurina_module_fritzing (saved by Fritzing 0.7.1b)
breadboards: 1

parts:
  IC1 = IC, DIP package, 24 pins [chip_label=IC spacing=300mil]
  LED1 = Purpurina Squared RGB Led (Common anode)
  LED2 = Purpurina Squared RGB Led (Common anode)
  LED3 = Purpurina Squared RGB Led (Common anode)
  LED4 = Purpurina Squared RGB Led (Common anode)
  LED5 = Purpurina Squared RGB Led (Common anode)
  LED6 = Purpurina Squared RGB Led (Common anode)
  IC2 = IC, DIP package, 24 pins [chip_label=IC spacing=300mil]
  LED11 = Purpurina Squared RGB Led (Common anode)
  LED10 = Purpurina Squared RGB Led (Common anode)
  LED8 = Purpurina Squared RGB Led (Common anode)
  LED9 = Purpurina Squared RGB Led (Common anode)
  LED7 = Purpurina Squared RGB Led (Common anode)
  IC3 = IC, DIP package, 24 pins [chip_label=IC spacing=300mil]
  LED12 = Purpurina Squared RGB Led (Common anode)
  LED13 = Purpurina Squared RGB Led (Common anode)
  LED14 = Purpurina Squared RGB Led (Common anode)
  LED15 = Purpurina Squared RGB Led (Common anode)
  LED16 = Purpurina Squared RGB Led (Common anode)
  R2 = Resistor [tolerance=±5% resistance=100 package=THT]
  R3 = Resistor [tolerance=±5% resistance=100 package=THT]
  R4 = Resistor [tolerance=±5% resistance=100 package=THT]
  J7 = shrouded pin header, 24 pins [form="♂ (shrouded male)" part_number=Input]
  J6 = shrouded pin header, 24 pins [form="♂ (shrouded male)" part_number=Output]

nets:
  N1: IC1.pin1, LED1.red_cathode
  N2: IC1.pin2, LED1.green
  N3: IC1.pin3, LED1.blue
  N4: IC1.pin4, LED2.red_cathode
  N5: IC1.pin5, LED2.green
  N6: IC1.pin6, LED2.blue
  N7: IC1.pin7, LED3.red_cathode
  N8: IC1.pin8, LED3.green
  N9: IC1.pin9, LED3.blue
  N10: IC1.pin10, LED4.red_cathode
  N11: IC1.pin11, LED4.green
  GND: IC1.pin12, IC2.pin12, IC3.pin12, J7.pin1, J6.pin24
  N12: IC1.pin13, LED4.blue
  N13: IC1.pin14, LED5.red_cathode
  N14: IC1.pin15, LED5.green
  N15: IC1.pin16, LED5.blue
  N16: IC1.pin17, LED6.red_cathode
  N17: IC1.pin18, IC2.pin18, IC3.pin18, J7.pin5
  N18: IC1.pin19, J7.pin2, J6.pin23
  N19: IC1.pin20, IC2.pin20, IC3.pin20, J7.pin21, J6.pin4
  N20: IC1.pin21, IC2.pin21, IC3.pin21, J7.pin20, J6.pin5
  N21: IC1.pin22, IC2.pin22, IC3.pin22, J7.pin4, J6.pin21
  N22: IC1.pin23, IC2.pin23, IC3.pin23, J7.pin3, J6.pin22
  5V: IC1.pin24, IC2.pin24, IC3.pin24, R2.Pin_0, R3.Pin_0, R4.Pin_0, J7.pin24, J6.pin1, J6.pin6
  N23: LED1.anode_(common), LED2.anode_(common), LED3.anode_(common), LED4.anode_(common), LED5.anode_(common), R2.Pin_1
  N24: LED6.blue, IC2.pin2
  N25: LED6.green, IC2.pin1
  N26: LED6.anode_(common), LED11.anode_(common), LED10.anode_(common), LED8.anode_(common), LED9.anode_(common), LED7.anode_(common), R3.Pin_1
  N27: IC2.pin3, LED7.red_cathode
  N28: IC2.pin4, LED7.green
  N29: IC2.pin5, LED7.blue
  N30: IC2.pin6, LED8.red_cathode
  N31: IC2.pin7, LED8.green
  N32: IC2.pin8, LED8.blue
  N33: IC2.pin9, LED9.red_cathode
  N34: IC2.pin10, LED9.green
  N35: IC2.pin11, LED9.blue
  N36: IC2.pin13, LED10.red_cathode
  N37: IC2.pin14, LED10.green
  N38: IC2.pin15, LED10.blue
  N39: IC2.pin16, LED11.red_cathode
  N40: IC2.pin17, LED11.green
  N41: IC2.pin19, J7.pin22, J6.pin3
  N42: LED11.blue, IC3.pin1
  N43: IC3.pin2, LED12.red_cathode
  N44: IC3.pin3, LED12.green
  N45: IC3.pin4, LED12.blue
  N46: IC3.pin5, LED13.red_cathode
  N47: IC3.pin6, LED13.green
  N48: IC3.pin7, LED13.blue
  N49: IC3.pin8, LED14.red_cathode
  N50: IC3.pin9, LED14.green
  N51: IC3.pin10, LED14.blue
  N52: IC3.pin11, LED15.red_cathode
  N53: IC3.pin13, LED15.green
  N54: IC3.pin14, LED15.blue
  N55: IC3.pin15, LED16.red_cathode
  N56: IC3.pin16, LED16.green
  N57: IC3.pin17, LED16.blue
  N58: IC3.pin19, J7.pin23, J6.pin2
  N59: LED12.anode_(common), LED13.anode_(common), LED14.anode_(common), LED15.anode_(common), LED16.anode_(common), R4.Pin_1
  N60: J7.pin6, J6.pin20
  N61: J7.pin7, J6.pin19
  N62: J7.pin8, J6.pin18
  N63: J7.pin9, J6.pin17
  N64: J7.pin10, J6.pin16
  N65: J7.pin11, J6.pin15
  N66: J7.pin12, J6.pin14
  N67: J7.pin13, J6.pin13
  N68: J7.pin14, J6.pin12
  N69: J7.pin15, J6.pin11
  N70: J7.pin16, J6.pin10
  N71: J7.pin17, J6.pin9
  N72: J7.pin18, J6.pin8
  N73: J7.pin19, J6.pin7

custom parts:
  Purpurina Squared RGB Led (Common anode): A full color SuperFlux LED.
