# Fritzing sketch purpurina_shield_fritzing (saved by Fritzing 0.7.4b)
breadboards: 1

parts:
  Arduino1 = Arduino
  IC2 = IC, DIP package, 24 pins [chip_label=IC spacing=300mil]
  R1 = Resistor [tolerance=±5% resistance=10k package=THT]
  R2 = Resistor [tolerance=±5% resistance=10k package=THT]
  R3 = Rotary Potentiometer (Large) [maximum_resistance=10kΩ package=THT]
  Output = DB25M
  J8 = female pin header, 3 pins [form="♀ (female)"]

nets:
  N1: Arduino1.GND, IC2.pin12, IC2.pin18, R1.Pin_1, R2.Pin_1, R3.leg1, Output.pin1
  N2: Arduino1.D13, Output.pin6
  N3: Arduino1.D12, Output.pin7
  N4: Arduino1.D11, Output.pin3
  N5: Arduino1.D10, Output.pin4
  N6: Arduino1.D9, Output.pin5
  N7: Arduino1.D8, Output.pin8
  N8: Arduino1.D7, Output.pin9
  N9: Arduino1.D6, IC2.pin23
  N10: Arduino1.D5, IC2.pin22
  N11: Arduino1.D4, IC2.pin21
  N12: Arduino1.D3, IC2.pin20
  N13: Arduino1.D2, IC2.pin19
  N14: Arduino1.+5V, IC2.pin24, R3.leg2, Output.pin2, J8.pin1
  N15: Arduino1.A0, R2.Pin_0, J8.pin3
  N16: Arduino1.A1, R1.Pin_0, J8.pin2
  N17: Arduino1.A2, R3.wiper
  N18: IC2.pin1, Output.pin10
  N19: IC2.pin2, Output.pin11
  N20: IC2.pin3, Output.pin12
  N21: IC2.pin4, Output.pin13
  N22: IC2.pin5, Output.pin14
  N23: IC2.pin6, Output.pin15
  N24: IC2.pin7, Output.pin16
  N25: IC2.pin8, Output.pin17
  N26: IC2.pin9, Output.pin18
  N27: IC2.pin10, Output.pin19
  N28: IC2.pin11, Output.pin20
  N29: IC2.pin13, Output.pin21
  N30: IC2.pin14, Output.pin22
  N31: IC2.pin15, Output.pin23
  N32: IC2.pin16, Output.pin24
  N33: IC2.pin17, Output.pin25

notes:
  Purpurina
  Alex Porto/2012
