# Fritzing sketch purpurina_module_fritzing (saved by Fritzing 0.7.4b)
breadboards: 1

parts:
  IC1 = IC, DIP package, 24 pins [chip_label=IC spacing=300mil]
  LED1 = Purpurina Squared RGB Led (Common anode)
  LED2 = Purpurina Squared RGB Led (Common anode)
  LED3 = Purpurina Squared RGB Led (Common anode)
  LED4 = Purpurina Squared RGB Led (Common anode)
  LED5 = Purpurina Squared RGB Led (Common anode)
  LED6 = Purpurina Squared RGB Led (Common anode)
  IC2 = IC, DIP package, 24 pins [chip_label=IC spacing=300mil]
  LED11 = Purpurina Squared RGB Led (Common anode)
  LED10 = Purpurina Squared RGB Led (Common anode)
  LED8 = Purpurina Squared RGB Led (Common anode)
  LED9 = Purpurina Squared RGB Led (Common anode)
  LED7 = Purpurina Squared RGB Led (Common anode)
  IC3 = IC, DIP package, 24 pins [chip_label=IC spacing=300mil]
  LED12 = Purpurina Squared RGB Led (Common anode)
  LED13 = Purpurina Squared RGB Led (Common anode)
  LED14 = Purpurina Squared RGB Led (Common anode)
  LED15 = Purpurina Squared RGB Led (Common anode)
  LED16 = Purpurina Squared RGB Led (Common anode)
  R2 = Resistor [tolerance=±5% resistance=100 package=THT]
  R3 = Resistor [tolerance=±5% resistance=100 package=THT]
  R4 = Resistor [tolerance=±5% resistance=100 package=THT]
  Input = DB25F
  Output = DB25M

nets:
  N1: IC1.pin1, LED1.red_cathode
  N2: IC1.pin2, LED1.green
  N3: IC1.pin3, LED1.blue
  N4: IC1.pin4, LED2.red_cathode
  N5: IC1.pin5, LED2.green
  N6: IC1.pin6, LED2.blue
  N7: IC1.pin7, LED3.red_cathode
  N8: IC1.pin8, LED3.green
  N9: IC1.pin9, LED3.blue
  N10: IC1.pin10, LED4.red_cathode
  N11: IC1.pin11, LED4.green
  GND: IC1.pin12, IC2.pin12, IC3.pin12, Input.pin1, Output.pin1
  N12: IC1.pin13, LED4.blue
  N13: IC1.pin14, LED5.red_cathode
  N14: IC1.pin15, LED5.green
  N15: IC1.pin16, LED5.blue
  N16: IC1.pin17, LED6.red_cathode
  N17: IC1.pin18, IC2.pin18, IC3.pin18, Input.pin10
  N18: IC1.pin19, Input.pin3, Output.pin3
  N19: IC1.pin20, IC2.pin20, IC3.pin20, Input.pin9, Output.pin9
  N20: IC1.pin21, IC2.pin21, IC3.pin21, Input.pin8, Output.pin8
  N21: IC1.pin22, IC2.pin22, IC3.pin22, Input.pin7, Output.pin7
  N22: IC1.pin23, IC2.pin23, IC3.pin23, Input.pin6, Output.pin6
  5V: IC1.pin24, IC2.pin24, IC3.pin24, R2.Pin_0, R3.Pin_0, R4.Pin_0, Input.pin2, Output.pin2, Output.pin25
  N23: LED1.anode_(common), LED2.anode_(common), LED3.anode_(common), LED4.anode_(common), LED5.anode_(common), R2.Pin_1
  N24: LED6.blue, IC2.pin2
  N25: LED6.green, IC2.pin1
  N26: LED6.anode_(common), LED11.anode_(common), LED10.anode_(common), LED8.anode_(common), LED9.anode_(common), LED7.anode_(common), R3.Pin_1
  N27: IC2.pin3, LED7.red_cathode
  N28: IC2.pin4, LED7.green
  N29: IC2.pin5, LED7.blue
  N30: IC2.pin6, LED8.red_cathode
  N31: IC2.pin7, LED8.green
  N32: IC2.pin8, LED8.blue
  N33: IC2.pin9, LED9.red_cathode
  N34: IC2.pin10, LED9.green
  N35: IC2.pin11, LED9.blue
  N36: IC2.pin13, LED10.red_cathode
  N37: IC2.pin14, LED10.green
  N38: IC2.pin15, LED10.blue
  N39: IC2.pin16, LED11.red_cathode
  N40: IC2.pin17, LED11.green
  N41: IC2.pin19, Input.pin4, Output.pin4
  N42: LED11.blue, IC3.pin1
  N43: IC3.pin2, LED12.red_cathode
  N44: IC3.pin3, LED12.green
  N45: IC3.pin4, LED12.blue
  N46: IC3.pin5, LED13.red_cathode
  N47: IC3.pin6, LED13.green
  N48: IC3.pin7, LED13.blue
  N49: IC3.pin8, LED14.red_cathode
  N50: IC3.pin9, LED14.green
  N51: IC3.pin10, LED14.blue
  N52: IC3.pin11, LED15.red_cathode
  N53: IC3.pin13, LED15.green
  N54: IC3.pin14, LED15.blue
  N55: IC3.pin15, LED16.red_cathode
  N56: IC3.pin16, LED16.green
  N57: IC3.pin17, LED16.blue
  N58: IC3.pin19, Input.pin5, Output.pin5
  N59: LED12.anode_(common), LED13.anode_(common), LED14.anode_(common), LED15.anode_(common), LED16.anode_(common), R4.Pin_1
  N60: Input.pin11, Output.pin10
  N61: Input.pin12, Output.pin11
  N62: Input.pin13, Output.pin12
  N63: Input.pin14, Output.pin13
  N64: Input.pin15, Output.pin14
  N65: Input.pin16, Output.pin15
  N66: Input.pin17, Output.pin16
  N67: Input.pin18, Output.pin17
  N68: Input.pin19, Output.pin18
  N69: Input.pin20, Output.pin19
  N70: Input.pin21, Output.pin20
  N71: Input.pin22, Output.pin21
  N72: Input.pin23, Output.pin22
  N73: Input.pin24, Output.pin23
  N74: Input.pin25, Output.pin24

custom parts:
  Purpurina Squared RGB Led (Common anode): A full color SuperFlux LED.
