# Fritzing sketch purpurina_shield_fritzing (saved by Fritzing 0.7.1b)
breadboards: 1

parts:
  Arduino1 = Arduino
  IC2 = IC, DIP package, 24 pins [chip_label=IC spacing=300mil]
  J7 = shrouded pin header, 24 pins [form="♂ (shrouded male)" part_number=Output]
  R1 = Resistor [tolerance=±5% resistance=10k package=THT]
  R2 = Resistor [tolerance=±5% resistance=10k package=THT]
  J8 = female pin header, 3 pins [form="♀ (female)"]

nets:
  N1: Arduino1.GND, IC2.pin12, IC2.pin18, J7.pin24, R1.Pin_1, R2.Pin_1
  N2: Arduino1.D13, J7.pin4
  N3: Arduino1.D12, J7.pin5
  N4: Arduino1.D11, J7.pin2
  N5: Arduino1.D10, J7.pin3
  N6: Arduino1.D9, J7.pin23
  N7: Arduino1.D8, J7.pin21
  N8: Arduino1.D7, J7.pin22
  N9: Arduino1.D6, IC2.pin20
  N10: Arduino1.D5, IC2.pin21
  N11: Arduino1.D4, IC2.pin22
  N12: Arduino1.D3, IC2.pin23
  N13: Arduino1.D2, IC2.pin19
  N14: Arduino1.+5V, IC2.pin24, J7.pin1, J8.pin2
  N15: Arduino1.A0, R2.Pin_0, J8.pin3
  N16: Arduino1.A1, R1.Pin_0, J8.pin1
  N17: IC2.pin1, J7.pin20
  N18: IC2.pin2, J7.pin19
  N19: IC2.pin3, J7.pin18
  N20: IC2.pin4, J7.pin17
  N21: IC2.pin5, J7.pin16
  N22: IC2.pin6, J7.pin15
  N23: IC2.pin7, J7.pin14
  N24: IC2.pin8, J7.pin13
  N25: IC2.pin9, J7.pin12
  N26: IC2.pin10, J7.pin11
  N27: IC2.pin11, J7.pin10
  N28: IC2.pin13, J7.pin9
  N29: IC2.pin14, J7.pin8
  N30: IC2.pin15, J7.pin7
  N31: IC2.pin16, J7.pin6
